# Fritzing sketch IR (saved by Fritzing 0.9.3b)
breadboards: 1

parts:
  パーツ1 = Arduino Uno (Rev3)
  LED1 = LED - 5mm [color="Infrared (940nm)" package="5 mm [THT]"]
  LED2 = LED - 5mm [color="Infrared (940nm)" package="5 mm [THT]"]
  LED3 = LED - 5mm [color="Infrared (940nm)" package="5 mm [THT]"]
  R1 = Resistor [tolerance=±5% resistance=100 package=THT]
  R2 = Resistor [tolerance=±5% resistance=100 package=THT]
  R3 = Resistor [tolerance=±5% resistance=100 package=THT]
  Q1 = NPN-Transistor [package="TO92 [THT]"]
  R4 = Resistor [tolerance=±5% resistance=4.7k package=THT]
  パーツ2 = Infra red receiver

nets (from the schematic view):
  N1: パーツ1.D11_PWM/MOSI, パーツ2.Data
  GND: パーツ1.GND, LED1.anode, Q1.E, パーツ2.GND
  N2: パーツ1.D3_PWM, R4.Pin_0
  5V: パーツ1.5V, パーツ2.VCC
  N3: LED1.cathode, R1.Pin_0
  N4: LED2.cathode, R2.Pin_0
  N5: LED3.cathode, R3.Pin_1
  N6: R1.Pin_1, R2.Pin_1, R3.Pin_0, Q1.B
  N7: Q1.C, R4.Pin_1
